# Fritzing sketch universal_pilot (saved by Fritzing 0.9.5d)

parts:
  Part1 = NRF24L01+ Breakout Board
  Part2 = Arduino Nano (Rev3.0) (ICSP)
  Part3 = Thumb Joystick
  Part4 = Thumb Joystick
  R1 = Rotary Potentiometer (Large) [maximum_resistance=100kΩ package=THT]
  R2 = Rotary Potentiometer (Large) [maximum_resistance=100kΩ package=THT]
  C1 = Capacitor Polarized [package=cpol-radial-10uf-25v]

nets:
  GND: Part1.GND, Part2.GND, Part3.GND, Part4.GND, R1.leg2, R2.leg2, C1.-
  VCC: Part1.VCC, Part2.3V3, C1.+
  N1: Part1.CE, Part2.D9
  N2: Part1.CS, Part2.D10
  N3: Part1.SCK, Part2.D13/SCK
  N4: Part1.MOSI, Part2.D11/MOSI
  N5: Part1.MISO, Part2.D12/MISO
  N6: Part2.D7, Part3.SEL
  N7: Part2.D8, Part4.SEL
  VCC_2: Part2.5V, Part3.VCC, Part4.VCC, R1.leg1, R2.leg1
  N8: Part2.A5, R2.wiper
  N9: Part2.A4, R1.wiper
  N10: Part2.A3, Part3.VERT
  N11: Part2.A2, Part3.HORZ
  N12: Part2.A1, Part4.VERT
  N13: Part2.A0, Part4.HORZ
